# Fritzing sketch DiseñoV1 (saved by Fritzing 0.9.3b)
breadboards: 1

parts:
  Componente1 = Arduino Uno (Rev3)
  Componente2 = HX711 Weighing Sensor Module
  Componente3 = SparkFun Load Sensor Combinator
  R1 = Rotary Potentiometer (Small) [maximum_resistance=100kΩ package=THT]
  VCC1 = Battery

nets:
  N1: Componente1.A0, Componente2.DO/RX
  N2: Componente1.A1, Componente2.CK/TX
  3V3: Componente1.3V3, Componente2.VCC, Componente3.5V, R1.wiper
  GND: Componente1.GND, Componente2.GND, Componente3.GND, R1.leg2, VCC1.-
  N3: Componente2.E+, Componente3.E+
  N4: Componente2.E-, Componente3.E-
  N5: Componente2.A+, Componente3.A-
  N6: Componente2.A-, Componente3.A+
  N7: R1.leg1, VCC1.+

notes:
  El dispositivo de arduino lleva integrado el Thinxtra usado para comunicación del dispositivo IoT.
  Sensor de Peso
  HX711
  +9V
  o
  +12V
  0V
  Potenciometro:
  Sirve para obtener el voltaje requerido con el cual va a funcionar el circuito.
